// Logisim project MIPS32.circ as structural Verilog
module MIPS32 (
);

  wire ALUuse, c1_out, RegWrite;
  wire [1:0] EXCtrl_q, PC_q, WBCtrl0_q, WBCtrl1_q, WBCtrl2_q;
  wire [2:0] MEMCtrl0_q, OP321;
  wire [4:0] Dest0_q, Instruction_q, Instruction_q_2, Instruction_q_5, Instruction_q_6, multiplexer_3_out,
       Rd_q, RegDest, Rt_q;
  wire [5:0] Instruction_q_3, Instruction_q_4;
  wire [29:0] incrementer_1_p2, PC_q_2;
  wire [31:0] A_q, ALUresult1_q, ALUresultD_q, B_q, bit_extender_1_out, bit_extender_2_out, Imm_q, MEMdata_q,
       mips_alu_1_p3, mipsprogramrom_1_p2, multiplexer_1_out, multiplexer_2_out, multiplexer_4_out,
       nacalculator_1_p4, PC4DE_q, PC4EM_q, PC4FD_q, registerfile_1_p6, registerfile_1_p7, WBdata;

  Clock c1 (.out(c1_out));
  Register #(.width(32), .trigger("falling")) PC (
    .D({incrementer_1_p2, PC_q}), .clk(c1_out), .Q({PC_q_2, PC_q}));  // open: en, clr
  // Incrementer #(.width(30)) incrementer_1: pin names not known; wires that end beside it: PC_q_2, incrementer_1_p2
  // MIPSProgramROM mipsprogramrom_1: pin names not known; wires that end beside it: {PC_q_2, PC_q}, mipsprogramrom_1_p2
  Register #(.width(32), .trigger("falling")) PC4FD (
    .D({incrementer_1_p2, PC_q}), .clk(c1_out), .Q(PC4FD_q));  // open: en, clr
  Register #(.width(32), .trigger("falling")) Instruction (
    .D(mipsprogramrom_1_p2), .clk(c1_out),
    .Q({Instruction_q_3, Instruction_q_2, Instruction_q, Instruction_q_6, Instruction_q_5, Instruction_q_4}));  // open: en, clr
  // RegisterFile registerfile_1: pin names not known; wires that end beside it: WBdata, RegWrite, RegDest, Instruction_q_2, Instruction_q, registerfile_1_p6, registerfile_1_p7
  assign bit_extender_1_out = {{16{1'b0}}, {Instruction_q_6, Instruction_q_5, Instruction_q_4}};  // Bit_Extender bit_extender_1
  Multiplexer #(.width(32), .enable("false")) multiplexer_1 (
    .in0(bit_extender_1_out), .in1(bit_extender_2_out), .out(multiplexer_1_out));  // open: sel
  assign bit_extender_2_out = {{16{Instruction_q_6[4]}}, {Instruction_q_6, Instruction_q_5, Instruction_q_4}};  // Bit_Extender bit_extender_2
  Register #(.width(6), .trigger("falling")) Func ();  // open: D, en, Q, clk, clr
  Register #(.width(32), .trigger("falling")) PC4DE (.D(PC4FD_q), .clk(c1_out), .Q(PC4DE_q));  // open: en, clr
  Register #(.width(32), .trigger("falling")) A (.D(registerfile_1_p6), .clk(c1_out), .Q(A_q));  // open: en, clr
  Register #(.width(32), .trigger("falling")) B (.D(registerfile_1_p7), .clk(c1_out), .Q(B_q));  // open: en, clr
  Register #(.width(32), .trigger("falling")) Imm (.D(multiplexer_1_out), .clk(c1_out), .Q(Imm_q));  // open: en, clr
  Register #(.width(5), .trigger("falling")) Rd (.D(Instruction_q_6), .clk(c1_out), .Q(Rd_q));  // open: en, clr
  Register #(.width(5), .trigger("falling")) Rt (.D(Instruction_q), .clk(c1_out), .Q(Rt_q));  // open: en, clr
  Register #(.width(6), .trigger("falling")) EXCtrl (.clk(c1_out), .Q({ALUuse, OP321, EXCtrl_q}));  // open: D, en, clr
  Register #(.width(3), .trigger("falling")) MEMCtrl0 (.clk(c1_out), .Q(MEMCtrl0_q));  // open: D, en, clr
  Register #(.width(2), .trigger("falling")) WBCtrl0 (.clk(c1_out), .Q(WBCtrl0_q));  // open: D, en, clr
  Multiplexer #(.width(32), .enable("false")) multiplexer_2 (
    .in0(B_q), .in1(Imm_q), .out(multiplexer_2_out), .sel(EXCtrl_q[1]));
  Multiplexer #(.width(5), .enable("false")) multiplexer_3 (
    .in0(Rd_q), .in1(Rt_q), .out(multiplexer_3_out), .sel(EXCtrl_q[0]));
  // Mips_ALU mips_alu_1: pin names not known; wires that end beside it: A_q, multiplexer_2_out, mips_alu_1_p3
  // NACalculator nacalculator_1: pin names not known; wires that end beside it: OP321, A_q, multiplexer_2_out, nacalculator_1_p4
  Multiplexer #(.width(32), .enable("false")) multiplexer_4 (
    .in0(mips_alu_1_p3), .in1(nacalculator_1_p4), .out(multiplexer_4_out), .sel(ALUuse));
  Register #(.width(32), .trigger("falling")) PC4EM (.D(PC4DE_q), .clk(c1_out), .Q(PC4EM_q));  // open: en, clr
  Register #(.width(32), .trigger("falling")) ALUresultD (
    .D(multiplexer_4_out), .clk(c1_out), .Q(ALUresultD_q));  // open: en, clr
  Register #(.width(32), .trigger("falling")) Bdata (.D(B_q));  // open: en, clk, Q, clr
  Register #(.width(5), .trigger("falling")) Dest0 (.D(multiplexer_3_out), .clk(c1_out), .Q(Dest0_q));  // open: en, clr
  Register #(.width(3), .trigger("falling")) MEMCtrl1 (.D(MEMCtrl0_q), .clk(c1_out));  // open: en, Q, clr
  Register #(.width(2), .trigger("falling")) WBCtrl1 (.D(WBCtrl0_q), .clk(c1_out), .Q(WBCtrl1_q));  // open: en, clr
  // MIPS_RAM mips_ram_1: pin names not known
  Register #(.width(32), .trigger("falling")) PC4MW (.D(PC4EM_q), .clk(c1_out));  // open: en, Q, clr
  Register #(.width(32), .trigger("falling")) ALUresult1 (
    .D(ALUresultD_q), .clk(c1_out), .Q(ALUresult1_q));  // open: en, clr
  Register #(.width(32), .trigger("falling")) MEMdata (.clk(c1_out), .Q(MEMdata_q));  // open: D, en, clr
  Register #(.width(5), .trigger("falling")) Dest1 (.D(Dest0_q), .clk(c1_out), .Q(RegDest));  // open: en, clr
  Register #(.width(2), .trigger("falling")) WBCtrl2 (.D(WBCtrl1_q), .clk(c1_out), .Q(WBCtrl2_q));  // open: en, clr
  Multiplexer #(.width(32), .enable("false")) multiplexer_5 (
    .in0(ALUresult1_q), .in1(MEMdata_q), .out(WBdata));  // open: sel

  // Notes on the sheet:
  //   IF stage
  //   contents of mipsprogramrom_1 (hex, n*v repeats v):
  //   ADDIU $1,$10,-1001 ANDI $10,$10,1001 ORI $10,$10,1001 XORI $10,$10,1001
  //   ID stage
  //   EX stage
  //   MEM stage
  //   WB stage
endmodule

module Control (
  input  in_1,
  input  in_2,
  input  in_3,
  input  in_4,
  input  in_5,
  input  in_6,
  output out_7,
  output out_8,
  output out_9,
  output out_10,
  output out_11,
  output out_12,
  output out_13,
  output out_14,
  output out_15
);
endmodule

module NACalculator (
  input  [31:0] A,
  input  [31:0] B,
  input  [2:0] OP321,
  input  [5:0] Func,
  output [31:0] V
);


  assign V = A;
endmodule
